# Fritzing sketch Antifurto (saved by Fritzing 0.8.3b)
breadboards: 1

parts:
  Arduino1 = Arduino
  Componente1 = Arduino Cellular Shield
  Power_plug1 = Power plug
  K_GSM = Relay [part_number=FRS1B-S package=THT]
  K_sirena = Relay [part_number=FRS1B-S package=THT]
  S1 = Pushbutton [package=THT]
  J1 = Piezo Speaker
  Nokia_5110_LCD_Module1 = Nokia5110LCDModule  # not connected
  IR1 = Infrared Proximity Sensor
  S2 = Pushbutton [package=THT]
  S3 = Pushbutton [package=THT]
  R1 = Resistor [tolerance=±5% resistance=10k package=THT]  # not connected
  R2 = Resistor [tolerance=±5% resistance=10k package=THT]  # not connected
  R3 = Resistor [tolerance=±5% resistance=10k package=THT]  # not connected
  R4 = Resistor [tolerance=±5% resistance=10k package=THT]  # not connected
  R5 = Resistor [tolerance=±5% resistance=100 package=THT]  # not connected

nets:
  GND: Arduino1.GND, Componente1.GND, Power_plug1.GND, K_GSM.COIL1, S1.leg0, J1.pin1, IR1.GND, S2.leg0, S3.leg0
  N1: Arduino1.D8, S2.leg1
  N2: Arduino1.D7, S1.leg1
  N3: Arduino1.D6, K_sirena.B
  N4: Arduino1.D5, J1.pin2
  N5: Arduino1.D4, S3.leg1
  N6: Arduino1.D3, Componente1.TX-O
  N7: Arduino1.D2, Componente1.RX-I
  VCC: Arduino1.+5V, Power_plug1.VCC, K_GSM.C1, K_GSM.C2, IR1.Vcc
  N8: Arduino1.A0, K_GSM.COIL2
  N9: Arduino1.A5, IR1.Vout
  N10: Componente1.5V, K_GSM.B
  N11: K_sirena.C1, K_sirena.C2

custom parts:
  : Nokia 5110 LCD with 8 pin. It's a 45mm*45mm module part. Description: The Nokia 5110 is a basic graphic LCD screen for lots of applications. It was originally intended for as a cell phone screen. This one is mounted on an easy to solder PCB. It uses the PCD8544 controller. The PCD8544 is a low power CMOS LCD controller/driver, designed to drive a graphic display of 48 rows and 84 columns. All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
