# Fritzing sketch giardino2015 (saved by Fritzing 0.9.1b)
breadboards: 1

parts:
  Nokia_5110_LCD_Module2 = Nokia5110LCDModule
  Componente1 = Arduino Uno (Rev3)
  R1-fotodiodo-luce-notturna = PHOTOCELL [package=photocell]
  S1-attiva_luce_notturna = SPST Switch [package=switch-spdt-smd]
  U1-Sirena = RELAY [package=relay-jzc]
  U2-Luce_notturna = RELAY [package=relay-jzc]
  S3-NC-contatto = SWITCH-MOMENTARY-2 [package=reed_switch_pth]
  R1 = Resistor [tolerance=±5% resistance=10k package="1206 [SMD]"]
  S4-NC-contatto = SWITCH-MOMENTARY-2 [package=reed_switch_pth]
  S2-NC-contatato_ritardato = SWITCH-MOMENTARY-2 [package=reed_switch_plastic]
  R2 = Resistor [tolerance=±5% resistance=10k package="0603 [SMD]"]
  R3-SDIN = Resistor [tolerance=±5% resistance=10k package="0603 [SMD]"]
  R4_D/C = Resistor [tolerance=±5% resistance=10k package="0603 [SMD]"]
  R5-RST = Resistor [tolerance=±5% resistance=10k package="0603 [SMD]"]
  R6-SCE = Resistor [tolerance=±5% resistance=10k package="0603 [SMD]"]
  R7_BL = Resistor [tolerance=±5% resistance=100 package="0603 [SMD]"]

nets:
  VCC: Nokia_5110_LCD_Module2.Vcc, Componente1.3V3
  N1: Nokia_5110_LCD_Module2.Grnd, U1-Sirena.COIL2, U2-Luce_notturna.COIL1, S3-NC-contatto.1, S4-NC-contatto.1, S2-NC-contatato_ritardato.1
  N2: Nokia_5110_LCD_Module2.SCE, R6-SCE.Pin_1
  N3: Nokia_5110_LCD_Module2.RST, R5-RST.Pin_1
  N4: Nokia_5110_LCD_Module2.D/C, R4_D/C.Pin_1
  N5: Nokia_5110_LCD_Module2.6_DN_(MOSI), R3-SDIN.Pin_1
  N6: Nokia_5110_LCD_Module2.SCLK, R2.Pin_1
  N7: Nokia_5110_LCD_Module2.LED, R7_BL.Pin_1
  N8: Componente1.A0, R1-fotodiodo-luce-notturna.P$1, S1-attiva_luce_notturna.P, R1.Pin_0
  N9: Componente1.D8, S2-NC-contatato_ritardato.2
  N10: Componente1.D9_PWM, S3-NC-contatto.2
  N11: Componente1.D10_PWM/SS, S4-NC-contatto.2
  N12: Componente1.D11_PWM/MOSI, U1-Sirena.COIL1
  N13: Componente1.D12/MISO, U2-Luce_notturna.COIL2
  N14: Componente1.D3_PWM, R2.Pin_0
  N15: Componente1.D4, R3-SDIN.Pin_0
  N16: Componente1.D5_PWM, R4_D/C.Pin_0
  N17: Componente1.D6_PWM, R5-RST.Pin_0
  N18: Componente1.D7, R6-SCE.Pin_0
  N19: Componente1.5V, R1-fotodiodo-luce-notturna.P$2, S1-attiva_luce_notturna.O, R7_BL.Pin_0
  N20: Componente1.GND, R1.Pin_1

custom parts:
  : Nokia 5110 LCD with 8 pin. It's a 45mm*45mm module part. Description: The Nokia 5110 is a basic graphic LCD screen for lots of applications. It was originally intended for as a cell phone screen. This one is mounted on an easy to solder PCB. It uses the PCD8544 controller. The PCD8544 is a low power CMOS LCD controller/driver, designed to drive a graphic display of 48 rows and 84 columns. All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

// code stored in the sketch: antifurto1_0.ino
#include <SPI.h>
/* Antifuto giardino versione alpha 0.1
   comprende:
   1 display 5110
   3 ingressi NC a calamita
   1 foto resistenza per luce notturna
   2 rele per azionamento sirena e luce di cortesia
*/

unsigned long currentMillis = 0L;
/*5110 collegare resistenze 10K
http://forum.arduino.cc/index.php?topic=254284.0
BL 100ohm
*/
#define PIN_SCE   7 //Pin 3 on LCD
#define PIN_RESET 6 //Pin 4 on LCD
#define PIN_DC    5 //Pin 5 on LCD
#define PIN_SDIN  4 //Pin 6 on LCD
#define PIN_SCLK  3 //Pin 7 on LCD

//interuttori NC


//rele
#define PIN_RELE_SIRENA 11
#define PIN_RELE_LUCE_NOTTURNA 12

//fotoresistenza
/*
----------------------------------------------------

           PhotoR     10K
 +5    o---/\/\/--.--/\/\/---o GND
                  |
 Pin 0 o-----------

----------------------------------------------------
*/
int LIGHT_PIN = 0; //define a pin for Photo resistor
long sogliaGiornoNotte = 512;//da verificare con metodo empirico
long pollingPhotoR = 300000;//5 minuti
unsigned long previousMillisPhotoR = 0L;
unsigned long lastPowerON =0L;
unsigned long lastPowerOFF =0L;


/*Contatti magnetici normalmente chiusi*/
#define NC_CONT_1  8
#define NC_CONT_2  9
#define NC_CONT_3 10

/* array "zona" degli eventi di allarme
contiene il valore in millis degli eventi dei contatti NC                       
              d8 d9 d10 */
typedef struct 
{
  unsigned long eventMillis;
  boolean  consumato;
} zona ;

zona zonas[3];

//The DC pin tells the LCD if we are sending a command or data
#define LCD_C     LOW
#define LCD_D     HIGH


//You may find a different size screen, but this one is 84 by 48 pixels
#define LCD_X     84
#define LCD_Y     48

//This table contains the hex values that represent pixels
//for a font that is 5 pixels wide and 8 pixels high
static const byte ASCII[][5] =
{
 {0x00, 0x00, 0x00, 0x00, 0x00} // 20  
,{0x00, 0x00, 0x5f, 0x00, 0x00} // 21 !
,{0x00, 0x07, 0x00, 0x07, 0x00} // 22 "
,{0x14, 0x7f, 0x14, 0x7f, 0x14} // 23 #
,{0x24, 0x2a, 0x7f, 0x2a, 0x12} // 24 $
,{0x23, 0x13, 0x08, 0x64, 0x62} // 25 %
,{0x36, 0x49, 0x55, 0x22, 0x50} // 26 &
,{0x00, 0x05, 0x03, 0x00, 0x00} // 27 '
,{0x00, 0x1c, 0x22, 0x41, 0x00} // 28 (
,{0x00, 0x41, 0x22, 0x1c, 0x00} // 29 )
,{0x14, 0x08, 0x3e, 0x08, 0x14} // 2a *
,{0x08, 0x08, 0x3e, 0x08, 0x08} // 2b +
,{0x00, 0x50, 0x30, 0x00, 0x00} // 2c ,
,{0x08, 0x08, 0x08, 0x08, 0x08} // 2d -
,{0x00, 0x60, 0x60, 0x00, 0x00} // 2e .
,{0x20, 0x10, 0x08, 0x04, 0x02} // 2f /
,{0x3e, 0x51, 0x49, 0x45, 0x3e} // 30 0
,{0x00, 0x42, 0x7f, 0x40, 0x00} // 31 1
,{0x42, 0x61, 0x51, 0x49, 0x46} // 32 2
,{0x21, 0x41, 0x45, 0x4b, 0x31} // 33 3
,{0x18, 0x14, 0x12, 0x7f, 0x10} // 34 4
,{0x27, 0x45, 0x45, 0x45, 0x39} // 35 5
,{0x3c, 0x4a, 0x49, 0x49, 0x30} // 36 6
,{0x01, 0x71, 0x09, 0x05, 0x03} // 37 7
,{0x36, 0x49, 0x49, 0x49, 0x36} // 38 8
,{0x06, 0x49, 0x49, 0x29, 0x1e} // 39 9
,{0x00, 0x36, 0x36, 0x00, 0x00} // 3a :
,{0x00, 0x56, 0x36, 0x00, 0x00} // 3b ;
,{0x08, 0x14, 0x22, 0x41, 0x00} // 3c <
,{0x14, 0x14, 0x14, 0x14, 0x14} // 3d =
,{0x00, 0x41, 0x22, 0x14, 0x08} // 3e >
,{0x02, 0x01, 0x51, 0x09, 0x06} // 3f ?
,{0x32, 0x49, 0x79, 0x41, 0x3e} // 40 @
,{0x7e, 0x11, 0x11, 0x11, 0x7e} // 41 A
,{0x7f, 0x49, 0x49, 0x49, 0x36} // 42 B
,{0x3e, 0x41, 0x41, 0x41, 0x22} // 43 C
,{0x7f, 0x41, 0x41, 0x22, 0x1c} // 44 D
,{0x7f, 0x49, 0x49, 0x49, 0x41} // 45 E
,{0x7f, 0x09, 0x09, 0x09, 0x01} // 46 F
,{0x3e, 0x41, 0x49, 0x49, 0x7a} // 47 G
,{0x7f, 0x08, 0x08, 0x08, 0x7f} // 48 H
,{0x00, 0x41, 0x7f, 0x41, 0x00} // 49 I
,{0x20, 0x40, 0x41, 0x3f, 0x01} // 4a J
,{0x7f, 0x08, 0x14, 0x22, 0x41} // 4b K
,{0x7f, 0x40, 0x40, 0x40, 0x40} // 4c L
,{0x7f, 0x02, 0x0c, 0x02, 0x7f} // 4d M
,{0x7f, 0x04, 0x08, 0x10, 0x7f} // 4e N
,{0x3e, 0x41, 0x41, 0x41, 0x3e} // 4f O
,{0x7f, 0x09, 0x09, 0x09, 0x06} // 50 P
,{0x3e, 0x41, 0x51, 0x21, 0x5e} // 51 Q
,{0x7f, 0x09, 0x19, 0x29, 0x46} // 52 R
,{0x46, 0x49, 0x49, 0x49, 0x31} // 53 S
,{0x01, 0x01, 0x7f, 0x01, 0x01} // 54 T
,{0x3f, 0x40, 0x40, 0x40, 0x3f} // 55 U
,{0x1f, 0x20, 0x40, 0x20, 0x1f} // 56 V
,{0x3f, 0x40, 0x38, 0x40, 0x3f} // 57 W
,{0x63, 0x14, 0x08, 0x14, 0x63} // 58 X
,{0x07, 0x08, 0x70, 0x08, 0x07} // 59 Y
,{0x61, 0x51, 0x49, 0x45, 0x43} // 5a Z
,{0x00, 0x7f, 0x41, 0x41, 0x00} // 5b [
,{0x02, 0x04, 0x08, 0x10, 0x20} // 5c ¥
,{0x00, 0x41, 0x41, 0x7f, 0x00} // 5d ]
,{0x04, 0x02, 0x01, 0x02, 0x04} // 5e ^
,{0x40, 0x40, 0x40, 0x40, 0x40} // 5f _
,{0x00, 0x01, 0x02, 0x04, 0x00} // 60 `
,{0x20, 0x54, 0x54, 0x54, 0x78} // 61 a
,{0x7f, 0x48, 0x44, 0x44, 0x38} // 62 b
,{0x38, 0x44, 0x44, 0x44, 0x20} // 63 c
,{0x38, 0x44, 0x44, 0x48, 0x7f} // 64 d
,{0x38, 0x54, 0x54, 0x54, 0x18} // 65 e
,{0x08, 0x7e, 0x09, 0x01, 0x02} // 66 f
,{0x0c, 0x52, 0x52, 0x52, 0x3e} // 67 g
,{0x7f, 0x08, 0x04, 0x04, 0x78} // 68 h
,{0x00, 0x44, 0x7d, 0x40, 0x00} // 69 i
,{0x20, 0x40, 0x44, 0x3d, 0x00} // 6a j 
,{0x7f, 0x10, 0x28, 0x44, 0x00} // 6b k
,{0x00, 0x41, 0x7f, 0x40, 0x00} // 6c l
,{0x7c, 0x04, 0x18, 0x04, 0x78} // 6d m
,{0x7c, 0x08, 0x04, 0x04, 0x78} // 6e n
,{0x38, 0x44, 0x44, 0x44, 0x38} // 6f o
,{0x7c, 0x14, 0x14, 0x14, 0x08} // 70 p
,{0x08, 0x14, 0x14, 0x18, 0x7c} // 71 q
,{0x7c, 0x08, 0x04, 0x04, 0x08} // 72 r
,{0x48, 0x54, 0x54, 0x54, 0x20} // 73 s
,{0x04, 0x3f, 0x44, 0x40, 0x20} // 74 t
,{0x3c, 0x40, 0x40, 0x20, 0x7c} // 75 u
,{0x1c, 0x20, 0x40, 0x20, 0x1c} // 76 v
,{0x3c, 0x40, 0x30, 0x40, 0x3c} // 77 w
,{0x44, 0x28, 0x10, 0x28, 0x44} // 78 x
,{0x0c, 0x50, 0x50, 0x50, 0x3c} // 79 y
,{0x44, 0x64, 0x54, 0x4c, 0x44} // 7a z
,{0x00, 0x08, 0x36, 0x41, 0x00} // 7b {
,{0x00, 0x00, 0x7f, 0x00, 0x00} // 7c |
,{0x00, 0x41, 0x36, 0x08, 0x00} // 7d }
,{0x10, 0x08, 0x08, 0x10, 0x08} // 7e ←
,{0x78, 0x46, 0x41, 0x46, 0x78} // 7f →
};

void LcdCharacter(char character)
{
  LcdWrite(LCD_D, 0x00);
  for (int index = 0; index < 5; index++)
  {
    LcdWrite(LCD_D, ASCII[character - 0x20][index]);
  }
  LcdWrite(LCD_D, 0x00);
}

void LcdClear(void)
{
  for (int index = 0; index < LCD_X * LCD_Y / 8; index++)
  {
    LcdWrite(LCD_D, 0x00);
  }
}

void LcdInitialise(void)
{
  pinMode(PIN_SCE, OUTPUT);
  pinMode(PIN_RESET, OUTPUT);
  pinMode(PIN_DC, OUTPUT);
  pinMode(PIN_SDIN, OUTPUT);
  pinMode(PIN_SCLK, OUTPUT);
  digitalWrite(PIN_RESET, LOW);
  digitalWrite(PIN_RESET, HIGH);
  LcdWrite(LCD_C, 0x21 );  // LCD Extended Commands.
  LcdWrite(LCD_C, 0xB1 );  // Set LCD Vop (Contrast). 
  LcdWrite(LCD_C, 0x04 );  // Set Temp coefficent. //0x04
  LcdWrite(LCD_C, 0x14 );  // LCD bias mode 1:48. //0x13
  LcdWrite(LCD_C, 0x20 );  // LCD Basic Commands
  LcdWrite(LCD_C, 0x0C );  // LCD in normal mode.
}

void LcdString(char *characters)
{
  while (*characters)
  {
    LcdCharacter(*characters++);
  }
}

void LcdWrite(byte dc, byte data)
{
  digitalWrite(PIN_DC, dc);
  digitalWrite(PIN_SCE, LOW);
  shiftOut(PIN_SDIN, PIN_SCLK, MSBFIRST, data);
  digitalWrite(PIN_SCE, HIGH);
}

void resetVariabili(void){
   for (int i = 0; i < sizeof(zonas); i++) {
           zonas[i].eventMillis=0L;
           zonas[i].consumato=false;
        }
}

/* Questa funzione restituisce una stringa che riporta l'ora minuti e secondi dall'evento*/
String getTimebyMillis(long m){
  char evento[50];
  unsigned int seconds = 0; 
  unsigned int minutes = 0; 
  unsigned int hours = 0; 
  /* se valore in millis è negativo lo riporto a positivo*/
  if (m<0)
    m*=-1;
  seconds += m / 1000; 
  m = m % 1000; 
  minutes += seconds / 60; 
  seconds = seconds % 60; 
  hours += minutes / 60; 
  minutes = minutes % 60; 
  hours = hours % 24; 
  sprintf(evento,"Ore:%s Minuti:%s Secondi:%s",hours,minutes,seconds);
  return evento;
}

void setup(void)
{
  Serial.begin(9600);  //Begin serial communcation
  LcdInitialise();
  LcdClear();
  LcdString("Ciao!");
  
  // setto i contatti NC 
  pinMode(NC_CONT_1, INPUT);           // set pin to input
  digitalWrite(NC_CONT_1, HIGH);       // turn on pullup resistors
  pinMode(NC_CONT_2, INPUT);           // set pin to input
  digitalWrite(NC_CONT_2, HIGH);       // turn on pullup resistors
  pinMode(NC_CONT_3, INPUT);           // set pin to input
  digitalWrite(NC_CONT_3, HIGH);       // turn on pullup resistors
  
  // initialize the digital pin's as an output.
  pinMode(PIN_RELE_SIRENA, OUTPUT);            // Relay 1 
  pinMode(PIN_RELE_LUCE_NOTTURNA, OUTPUT);     // Relay 2

  resetVariabili();
}

void loop(void)
{
  currentMillis = millis();
  PhotoRes();
}

void PhotoRes(void){
  Serial.println(analogRead(LIGHT_PIN)); //Write the value of the photoresistor to the serial monitor.
   
  if(currentMillis - previousMillisPhotoR > pollingPhotoR) {
    // save the last time control
    previousMillisPhotoR = currentMillis;  

    if(analogRead(LIGHT_PIN)>sogliaGiornoNotte && lastPowerOFF >=lastPowerON ){
      // Accendo luce nottura soglia superata 
      digitalWrite(PIN_RELE_LUCE_NOTTURNA, HIGH);
      lastPowerON=previousMillisPhotoR;
    } else if(lastPowerON > lastPowerOFF){
      //spengo luce notturna
      digitalWrite(PIN_RELE_LUCE_NOTTURNA, LOW);
      lastPowerOFF=previousMillisPhotoR;
    }
  }
}
